# Fritzing sketch Keypad (saved by Fritzing 0.9.3b)
breadboards: 1

parts:
  Part1 = Arduino Uno (Rev3)
  S1 = Pushbutton [package="[THT]"]
  S2 = Pushbutton [package="[THT]"]
  S3 = Pushbutton [package="[THT]"]
  S4 = Pushbutton [package="[THT]"]
  S5 = Pushbutton [package="[THT]"]
  S6 = Pushbutton [package="[THT]"]
  S7 = Pushbutton [package="[THT]"]
  S8 = Pushbutton [package="[THT]"]
  S9 = Pushbutton [package="[THT]"]
  S10 = Pushbutton [package="[THT]"]
  S11 = Pushbutton [package="[THT]"]
  S12 = Pushbutton [package="[THT]"]
  LED1 = LED - 5mm [color="Red (633nm)" package="5 mm [THT]"]
  R1 = Resistor [tolerance=±5% resistance=220 package="2010 [SMD]"]

nets:
  N1: Part1.D8, S11.Pin_1, S11.Pin_2, S12.Pin_1, S12.Pin_2
  N2: Part1.D9_PWM, S5.Pin_1, S5.Pin_2, S10.Pin_1, S10.Pin_2
  N3: Part1.D10_PWM/SS, S4.Pin_1, S4.Pin_2, S9.Pin_1, S9.Pin_2
  N4: Part1.D11_PWM/MOSI, S3.Pin_1, S3.Pin_2, S8.Pin_1, S8.Pin_2
  N5: Part1.D12/MISO, S2.Pin_1, S2.Pin_2, S7.Pin_1, S7.Pin_2
  N6: Part1.D13/SCK, S1.Pin_1, S1.Pin_2, S6.Pin_1, S6.Pin_2
  N7: Part1.GND, LED1.cathode
  N8: Part1.D2, R1.Pin_1
  N9: Part1.D6_PWM, S6.Pin_3, S6.Pin_4, S7.Pin_3, S7.Pin_4, S8.Pin_3, S8.Pin_4, S9.Pin_3, S9.Pin_4, S10.Pin_3, S10.Pin_4, S12.Pin_3, S12.Pin_4
  N10: Part1.D7, S1.Pin_3, S1.Pin_4, S2.Pin_3, S2.Pin_4, S3.Pin_3, S3.Pin_4, S4.Pin_3, S4.Pin_4, S5.Pin_3, S5.Pin_4, S11.Pin_3, S11.Pin_4
  N11: LED1.anode, R1.Pin_0

notes:
  1
  2
  3
  4
  5
  6
  7
  8
  9
  0
  *
  #
